# Fritzing sketch smell_sensor (saved by Fritzing 0.9.1b)
breadboards: 1

parts:
  Composant1 = Arduino Nano (Rev3.0)
  Composant2 = Gas Sensor Breakout Board
  Composant3 = Gas Sensor Breakout Board
  DHT1 = DHT11 Humitidy and Temperature Sensor
  Composant4 = Adafruit FONA - Mini Cellular GSM Breakout
  R1 = Resistor [tolerance=±5% resistance=10k package="1206 [SMD]"]

nets (from the breadboard view):
  GND: Composant1.GND, Composant2.GND, Composant3.GND, DHT1.GND, Composant4.PWRKEY_5V, Composant4.GND
  N1: Composant1.D2, Composant4.RXD_5V
  N2: Composant1.D3, Composant4.TXD_5V
  N3: Composant1.D4, Composant4.RESET_5V
  N4: Composant1.D5, DHT1.DATA, R1.Pin_0
  5V: Composant1.5V, Composant2.H1, Composant3.B1, DHT1.VDD, R1.Pin_1
  N5: Composant1.A1, Composant2.A1
  N6: Composant1.A0, Composant3.H1
  N7: Composant1.3V3, Composant4.VCCIO

custom parts:
  DHT11 Humitidy and Temperature Sensor: DHT11 Humidity and Temperature Sensor
  Adafruit FONA - Mini Cellular GSM Breakout: An all-in-one cellular phone module that lets you add voice, text, SMS and GPRS data to your project. Quad-band 850/900/1800/1900MHz - connect onto any global GSM network with any 2G SIM. Includes an onboard LiPoly battery charging circuitry so you can take your project on the go. Also works as an FM radio receiver.
